// Logisim project 01_gates.circ as structural Verilog: 1 circuit, main circuit main
module main (
  input  in_1,
  input  in_2,
  input  in_3,
  input  in_4,
  input  in_5,
  input  in_6,
  input  OR,
  input  in_8,
  input  in_9,
  input  in_10,
  input  in_11,
  input  in_12,
  input  in_13,
  input  in_14,
  input  NOR,
  input  in_16,
  input  in_17,
  input  in_18
);

  wire and_1_out, nand_1_out, nor_1_out, not_1_out, or_1_out, transistor_1_out, transistor_2_out,
       transistor_4_out, transistor_7_out, transistor_8_out, transistor_11_out, transistor_12_out,
       transistor_15_out, transistor_16_out, transistor_19_out, transistor_21_out;

  Transistor #(.\type ("n")) transistor_1 (.in(1'b0), .out(transistor_1_out), .gate(NOR));
  Transistor transistor_2 (.in(1'b1), .out(transistor_2_out), .gate(in_2));
  Transistor #(.\type ("n")) transistor_3 (.in(1'b0), .out(transistor_2_out), .gate(in_2));
  Transistor transistor_4 (.in(1'b1), .out(transistor_4_out), .gate(in_14));
  Transistor transistor_5 (.in(1'b1), .out(transistor_4_out), .gate(in_10));
  Transistor #(.\type ("n")) transistor_6 (.in(transistor_7_out), .out(transistor_4_out), .gate(in_10));
  Transistor #(.\type ("n")) transistor_7 (.in(1'b0), .out(transistor_7_out), .gate(in_14));
  Transistor transistor_8 (.in(1'b1), .out(transistor_8_out), .gate(NOR));
  Transistor transistor_9 (.in(transistor_8_out), .out(transistor_1_out), .gate(in_16));
  Transistor #(.\type ("n")) transistor_10 (.in(1'b0), .out(transistor_1_out), .gate(in_16));
  LED led_1 (.in(transistor_2_out));
  LED led_2 (.in(transistor_4_out));
  LED led_3 (.in(transistor_1_out));
  not not_1 (not_1_out, in_3);
  LED led_4 (.in(not_1_out));
  nand nand_1 (nand_1_out, in_8, in_11);
  LED led_5 (.in(nand_1_out));
  nor nor_1 (nor_1_out, in_17, in_18);
  LED led_6 (.in(nor_1_out));
  Transistor transistor_11 (.in(1'b1), .out(transistor_11_out), .gate(in_6));
  Transistor #(.\type ("n")) transistor_12 (.in(1'b0), .out(transistor_12_out), .gate(OR));
  Transistor transistor_13 (.in(1'b1), .out(transistor_11_out), .gate(in_5));
  Transistor #(.\type ("n")) transistor_14 (.in(transistor_15_out), .out(transistor_11_out), .gate(in_5));
  Transistor #(.\type ("n")) transistor_15 (.in(1'b0), .out(transistor_15_out), .gate(in_6));
  Transistor transistor_16 (.in(1'b1), .out(transistor_16_out), .gate(OR));
  Transistor transistor_17 (.in(transistor_16_out), .out(transistor_12_out), .gate(in_12));
  Transistor #(.\type ("n")) transistor_18 (.in(1'b0), .out(transistor_12_out), .gate(in_12));
  Transistor transistor_19 (.in(1'b1), .out(transistor_19_out), .gate(transistor_11_out));
  LED led_7 (.in(transistor_19_out));
  Transistor #(.\type ("n")) transistor_20 (.in(1'b0), .out(transistor_19_out), .gate(transistor_11_out));
  Transistor transistor_21 (.in(1'b1), .out(transistor_21_out), .gate(transistor_12_out));
  Transistor #(.\type ("n")) transistor_22 (.in(1'b0), .out(transistor_21_out), .gate(transistor_12_out));
  LED led_8 (.in(transistor_21_out));
  and and_1 (and_1_out, in_1, in_4);
  or or_1 (or_1_out, in_9, in_13);
  LED led_9 (.in(and_1_out));
  LED led_10 (.in(or_1_out));

  // Notes on the sheet:
  //   NOT
  //   NAND
  //   AND
endmodule
